# Fritzing sketch circuit (saved by Fritzing 1.0.4)
breadboards: 1

parts:
  부품1 = Arduino Leonardo (Rev3b)
  부품5 = Rectangle Red LED Button
  부품6 = Rectangle Red LED Button
  부품7 = Rectangle Red LED Button
  부품8 = Rectangle Red LED Button
  부품9 = Rectangle Red LED Button
  부품10 = Rectangle Red LED Button
  부품12 = Rectangle Red LED Button
  부품13 = Rectangle Red LED Button
  부품14 = Rectangle Red LED Button
  부품15 = Rectangle Red LED Button

nets:
  N1: 부품1.D0/RX, 부품15.LED_-, 부품15.COM
  N2: 부품1.D1/TX, 부품14.LED_-, 부품14.COM
  N3: 부품1.D2/SDA, 부품12.LED_-, 부품12.COM
  N4: 부품1.D3_PWM/SCL, 부품13.LED_-, 부품13.COM
  N5: 부품1.D4/A6, 부품10.LED_-, 부품10.COM
  N6: 부품1.D5_PWM, 부품9.LED_-, 부품9.COM
  N7: 부품1.D6_PWM/A7, 부품8.LED_-, 부품8.COM
  N8: 부품1.D7, 부품7.LED_-, 부품7.COM
  N9: 부품1.5V, 부품5.LED_+, 부품6.LED_+, 부품7.LED_+, 부품8.LED_+, 부품9.LED_+, 부품10.LED_+, 부품12.LED_+, 부품13.LED_+, 부품14.LED_+, 부품15.LED_+
  N10: 부품1.GND, 부품5.NO, 부품6.NO, 부품7.NO, 부품8.NO, 부품9.NO, 부품10.NO, 부품12.NO, 부품13.NO, 부품14.NO, 부품15.NO
  N11: 부품1.D8/A8, 부품6.LED_-, 부품6.COM
  N12: 부품1.D9_PWM/A9, 부품5.LED_-, 부품5.COM

notes:
  Cyan: LED-
  Black: COM
  Blue: NO
  Red: LED+
  Green: Key Input

custom parts:
  Rectangle Red LED Button: Arcade LED Button for Rhythm Game (CWB 405) The CWB 405 button consists of a button, a switch, and an LED that can be separated. The button part presses a switch, so only the switch and LED pins are supported. It was written based on the 405 button set produced by IST (istmall.co.kr). - LED: 5V DC - Switch: GSM-V0303A06, Gersung Engineering Micro Switch V Type
