# Fritzing sketch controller (saved by Fritzing 1.0.4)
breadboards: 1

parts:
  부품2 = Arduino Leonardo (Rev3b)
  부품3 = Rectangle Red LED Button
  부품4 = Rectangle Red LED Button
  부품5 = Rectangle Red LED Button
  부품6 = Rectangle Red LED Button
  부품7 = Rectangle Red LED Button
  부품8 = Rectangle Red LED Button
  부품9 = Rectangle Red LED Button
  부품10 = Rectangle Red LED Button
  부품11 = Rectangle Red LED Button
  부품12 = Rectangle Red LED Button

nets:
  N1: 부품2.D0/RX, 부품3.COM
  N2: 부품2.D1/TX, 부품4.COM
  N3: 부품2.D2/SDA, 부품5.COM
  N4: 부품2.D3_PWM/SCL, 부품6.COM
  N5: 부품2.D4/A6, 부품7.COM
  N6: 부품2.D5_PWM, 부품8.COM
  N7: 부품2.D6_PWM/A7, 부품12.COM
  N8: 부품2.D7, 부품11.COM
  N9: 부품2.5V, 부품3.LED_+, 부품4.LED_+, 부품5.LED_+, 부품6.LED_+, 부품7.LED_+, 부품8.LED_+, 부품9.LED_+, 부품10.LED_+, 부품11.LED_+, 부품12.LED_+
  N10: 부품2.GND, 부품3.LED_-, 부품3.NO, 부품4.LED_-, 부품4.NO, 부품5.LED_-, 부품5.NO, 부품6.LED_-, 부품6.NO, 부품7.LED_-, 부품7.NO, 부품8.LED_-, 부품8.NO, 부품9.LED_-, 부품9.NO, 부품10.LED_-, 부품10.NO, 부품11.LED_-, 부품11.NO, 부품12.LED_-, 부품12.NO
  N11: 부품2.D8/A8, 부품10.COM
  N12: 부품2.D9_PWM/A9, 부품9.COM

custom parts:
  Rectangle Red LED Button: Arcade LED Button for Rhythm Game (CWB 405) The CWB 405 button consists of a button, a switch, and an LED that can be separated. The button part presses a switch, so only the switch and LED pins are supported. It was written based on the 405 button set produced by IST (istmall.co.kr). - LED: 5V DC - Switch: GSM-V0303A06, Gersung Engineering Micro Switch V Type
